# Fritzing sketch door-sensor (saved by Fritzing 0.9.10b)
circuit board: 9.42799cm x 4.53761cm
breadboards: 1

parts:
  IC1 = AE-TYBLE16 (300mil) [part_number=K-12339 package="DIP (Dual Inline) [THT]"]
  C1 = Capacitor Polarized [package=cpol-radial-100uf-25v]
  Q1 = LTR-301 [package=ltr-301]
  R1 = Resistor [tolerance=±5% power=0.25 resistance=1k package=THT]
  S1 = Toggle Switch [package=THT]
  S5 = Reed switch [package=THT]
  R2 = Resistor [tolerance=±5% power=0.25 resistance=1 package=THT]
  J3 = female pin header, 6 pins [form="♀ (female)"]
  J5 = female pin header, 2 pins [form="♀ (female)"]
  J6 = female pin header, 2 pins [form="♀ (female)"]
  J7 = female pin header, 2 pins [form="♀ (female)"]
  IC2 = IC, DIP package, 6 pins [chip_label=R3111N211A]
  LED1 = LED - 3mm [color="Red (633nm)" current=30mA package="3 mm [THT]"]
  R3 = Resistor [tolerance=±5% power=0.25 resistance=47 package=THT]
  R4 = Resistor [tolerance=±5% power=0.25 resistance=47 package=THT]
  S8 = Toggle Switch [package=THT]
  S7 = Toggle Switch [package=THT]
  S6 = Toggle Switch [package=THT]
  BAT1 = Battery Holders [package=battcon_245mm]
  LED2 = LED - 3mm [color="Green (565nm)" current=30mA package="3 mm [THT]"]

nets:
  N1: IC1.DIP2, J3.pin2
  N2: IC1.DIP3, J3.pin3
  N3: IC1.DIP5, J3.pin5
  N4: IC1.DIP6, J3.pin6
  N5: IC1.DIP9, Q1.E, R1.Pin_0
  N6: IC1.DIP10, R4.Pin_0
  N7: IC1.DIP13, C1.-, R1.Pin_1, J3.pin4, J5.pin2, IC2.pin3, BAT1.-, LED2.cathode
  N8: IC1.DIP14, C1.+, S1.L1, S1.COM, R2.Pin_0, J3.pin1, J7.pin2, IC2.pin2, LED1.anode, S7.L1, S7.COM
  N9: Q1.C, S1.L2
  N10: S5.pin_1, J6.pin1, S8.COM, S6.L2
  N11: S5.pin_2, R2.Pin_1, J6.pin2, J7.pin1, S7.L2, S6.L1, S6.COM
  N12: J5.pin1, S8.L1
  N13: IC2.pin1, R3.Pin_1
  N14: LED1.cathode, R3.Pin_0
  N15: R4.Pin_1, LED2.anode
  N16: S8.L2, BAT1.+

custom parts:
  AE-TYBLE16 (300mil): AE-TYBLE16 BLE module whose MPU core is nRF51822 as 300mil (7.62mm) breadfriendly width, actual width is 8.0mm
